# Fritzing sketch eighties_arp_wiring (saved by Fritzing 0.9.6b)
breadboards: 1

parts:
  R1 = Resistor Mini [tolerance=±5% resistance=1k package=THT]
  J1 = TRRS 3.5mm Jack Breakout
  S1 = Pushbutton [package="[SMD]"]
  S2 = Pushbutton [package="[SMD]"]
  POT2 = POT [package=alps_pot]
  R2 = Resistor Mini [tolerance=±5% resistance=1k package=THT]
  C2 = Electrolytic Capacitor [capacitance=10µF voltage=16V package="100 mil [THT, electrolytic]"]
  U1 = Adafruit QT Py [part_number="Adafruit #4600"]
  POT1 = POT [package=alps_pot]
  C1 = Ceramic Capacitor [capacitance=100nF voltage=35V package="100 mil [THT, multilayer]"]

nets:
  N1: R1.Pin_0, R2.Pin_1, C1.0
  N2: R1.Pin_1, J1.RING1, J1.TIP
  GND: J1.SLEEVE, S1.Pin_3, S1.Pin_4, S2.Pin_3, S2.Pin_4, POT2.E, U1.GND, POT1.E, C1.1
  N3: S1.Pin_1, S1.Pin_2, U1.RX
  N4: S2.Pin_1, S2.Pin_2, U1.TX
  N5: POT2.S, U1.A2
  3.3V: POT2.A, U1.3.3V, POT1.A
  N6: R2.Pin_0, C2.-
  N7: C2.+, U1.A0
  N8: U1.A1, POT1.S

custom parts:
  Resistor Mini: A generic resistor (0.25W)
  Adafruit QT Py: What a cutie pie! Or is it... a QT Py? This diminutive dev board comes with our favorite lil chip, the SAMD21 (as made famous in our GEMMA M0 and Trinket M0 boards). This time it comes with our favorite connector - the STEMMA QT, a chainable I2C port that can be used with any of our STEMMA QT sensors and accessories. OLEDs! Inertial Measurment Units! Sensors a-plenty. All plug-and-play thanks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
